// Logisim project 8bit_computer.circ as structural Verilog: 8 circuits, main circuit main
module main (
  input  OE_test,
  input  [3:0] OE_testing_data,
  input  [7:0] testingData,
  input  in_4,
  input  OEtestingData,
  input  InternalOE,
  input  [3:0] in_7,
  input  in_8,
  output [3:0] contentOfCounter,
  output [3:0] MARcontent,
  output [7:0] IRcontent,
  output [7:0] MBRcontent,
  output [7:0] regAcontent,
  output [7:0] ALUcontent,
  output [7:0] regBcontent,
  output [7:0] out_16
);

  wire clk_out, controlled_buffer_5_out, controlunit_1_aluoe, controlunit_1_aluwe, controlunit_1_awe,
       controlunit_1_bwe, controlunit_1_iroe, controlunit_1_irwe, controlunit_1_mbeoe, controlunit_1_mbrwe,
       controlunit_1_oemar, controlunit_1_oeram, controlunit_1_opoe, controlunit_1_opwe, controlunit_1_wemar,
       controlunit_1_weram, undriven;
  wire [3:0] controlled_buffer_1_out, counterforalu_1_out_3, mar_1_dout;
  wire [7:0] alu_1_dout, bit_extender_1_out, ram_1_dout, register8bit_1_dout, register8bit_5_dout;
  wire [15:0] decimaldecoder_5_dout, decimaldecoder_5_dout_2;
  wire [31:0] decimaldecoder_1_dout, decimaldecoder_2_dout, decimaldecoder_3_dout, decimaldecoder_4_dout;

  counterForALU counterforalu_1 (.in_1(in_7), .clk(clk_out), .out_3(counterforalu_1_out_3));
  controlUnit controlunit_1 (
    .en(in_4), .counter(contentOfCounter), .ce(counterforalu_1_out_3[3]), .co(counterforalu_1_out_3[2]),
    .en1(counterforalu_1_out_3[1]), .en0(counterforalu_1_out_3[0]), .sw(in_8), .weMAR(controlunit_1_wemar),
    .oeMAR(controlunit_1_oemar), .weRAM(controlunit_1_weram), .oeRAM(controlunit_1_oeram),
    .irWE(controlunit_1_irwe), .irOE(controlunit_1_iroe), .aWE(controlunit_1_awe), .bWE(controlunit_1_bwe),
    .aluWE(controlunit_1_aluwe), .aluOE(controlunit_1_aluoe), .mbrWE(controlunit_1_mbrwe),
    .mbeOE(controlunit_1_mbeoe), .opWE(controlunit_1_opwe), .opOE(controlunit_1_opoe));
  Clock clk (.out(clk_out));
  assign controlled_buffer_1_out = counterforalu_1_out_3[2] ? contentOfCounter : 4'bz;  // Controlled_Buffer controlled_buffer_1
  Counter #(.max('h4), .width(4)) programCounter (
    .D(controlled_buffer_1_out), .count(counterforalu_1_out_3[3]), .Q(contentOfCounter), .clk(clk_out));  // open: load, carry, up, clr
  register8bit register8bit_1 (
    .clk(clk_out), .we(controlunit_1_irwe), .de(alu_1_dout), .oe(controlunit_1_iroe),
    .Dout(register8bit_1_dout), .Dstored(IRcontent));
  register8bit register8bit_2 (
    .clk(clk_out), .we(controlunit_1_awe), .de(alu_1_dout), .Dstored(regAcontent));  // open: oe, Dout
  ALU alu_1 (
    .regA(regAcontent), .regB(regBcontent), .WE(controlunit_1_aluwe), .selectBits(alu_1_dout), .clk(clk_out),
    .OE(controlunit_1_aluoe), .Dout(alu_1_dout), .ALUresult(ALUcontent));
  register8bit register8bit_3 (
    .clk(clk_out), .we(controlunit_1_bwe), .de(alu_1_dout), .oe(undriven), .Dstored(regBcontent));  // open: Dout
  assign bit_extender_1_out = {{4{contentOfCounter[3]}}, contentOfCounter};  // Bit_Extender bit_extender_1
  decimalDecoder decimaldecoder_1 (.Din(regAcontent), .Dout(decimaldecoder_1_dout));
  _7_Segment_Display u_7_segment_display_1 (
    .g(decimaldecoder_2_dout[15]), .f(decimaldecoder_2_dout[14]), .a(decimaldecoder_2_dout[13]),
    .b(decimaldecoder_2_dout[12]), .e(decimaldecoder_2_dout[31]), .d(decimaldecoder_2_dout[30]),
    .c(decimaldecoder_2_dout[29]), .dp(decimaldecoder_2_dout[28]));
  decimalDecoder decimaldecoder_2 (.Din(ALUcontent), .Dout(decimaldecoder_2_dout));
  _7_Segment_Display u_7_segment_display_2 (
    .g(decimaldecoder_3_dout[15]), .f(decimaldecoder_3_dout[14]), .a(decimaldecoder_3_dout[13]),
    .b(decimaldecoder_3_dout[12]), .e(decimaldecoder_3_dout[31]), .d(decimaldecoder_3_dout[30]),
    .c(decimaldecoder_3_dout[29]), .dp(decimaldecoder_3_dout[28]));
  decimalDecoder decimaldecoder_3 (.Din(regBcontent), .Dout(decimaldecoder_3_dout));
  decimalDecoder decimaldecoder_4 (.Din(bit_extender_1_out), .Dout(decimaldecoder_4_dout));
  _7_Segment_Display u_7_segment_display_3 (
    .g(decimaldecoder_1_dout[15]), .f(decimaldecoder_1_dout[14]), .a(decimaldecoder_1_dout[13]),
    .b(decimaldecoder_1_dout[12]), .e(decimaldecoder_1_dout[31]), .d(decimaldecoder_1_dout[30]),
    .c(decimaldecoder_1_dout[29]), .dp(decimaldecoder_1_dout[28]));
  _7_Segment_Display u_7_segment_display_4 (
    .g(decimaldecoder_1_dout[11]), .f(decimaldecoder_1_dout[10]), .a(decimaldecoder_1_dout[9]),
    .b(decimaldecoder_1_dout[8]), .e(decimaldecoder_1_dout[27]), .d(decimaldecoder_1_dout[26]),
    .c(decimaldecoder_1_dout[25]), .dp(decimaldecoder_1_dout[24]));
  _7_Segment_Display u_7_segment_display_5 (
    .g(decimaldecoder_2_dout[11]), .f(decimaldecoder_2_dout[10]), .a(decimaldecoder_2_dout[9]),
    .b(decimaldecoder_2_dout[8]), .e(decimaldecoder_2_dout[27]), .d(decimaldecoder_2_dout[26]),
    .c(decimaldecoder_2_dout[25]), .dp(decimaldecoder_2_dout[24]));
  _7_Segment_Display u_7_segment_display_6 (
    .g(decimaldecoder_2_dout[7]), .f(decimaldecoder_2_dout[6]), .a(decimaldecoder_2_dout[5]),
    .b(decimaldecoder_2_dout[4]), .e(decimaldecoder_2_dout[23]), .d(decimaldecoder_2_dout[22]),
    .c(decimaldecoder_2_dout[21]), .dp(decimaldecoder_2_dout[20]));
  _7_Segment_Display u_7_segment_display_7 (
    .g(decimaldecoder_3_dout[11]), .f(decimaldecoder_3_dout[10]), .a(decimaldecoder_3_dout[9]),
    .b(decimaldecoder_3_dout[8]), .e(decimaldecoder_3_dout[27]), .d(decimaldecoder_3_dout[26]),
    .c(decimaldecoder_3_dout[25]), .dp(decimaldecoder_3_dout[24]));
  _7_Segment_Display u_7_segment_display_8 (
    .g(decimaldecoder_3_dout[7]), .f(decimaldecoder_3_dout[6]), .a(decimaldecoder_3_dout[5]),
    .b(decimaldecoder_3_dout[4]), .e(decimaldecoder_3_dout[23]), .d(decimaldecoder_3_dout[22]),
    .c(decimaldecoder_3_dout[21]), .dp(decimaldecoder_3_dout[20]));
  _7_Segment_Display u_7_segment_display_9 (
    .g(decimaldecoder_4_dout[3]), .f(decimaldecoder_4_dout[2]), .a(decimaldecoder_4_dout[1]),
    .b(decimaldecoder_4_dout[0]), .e(decimaldecoder_4_dout[19]), .d(decimaldecoder_4_dout[18]),
    .c(decimaldecoder_4_dout[17]), .dp(decimaldecoder_4_dout[16]));
  _7_Segment_Display u_7_segment_display_10 (
    .g(decimaldecoder_1_dout[7]), .f(decimaldecoder_1_dout[6]), .a(decimaldecoder_1_dout[5]),
    .b(decimaldecoder_1_dout[4]), .e(decimaldecoder_1_dout[23]), .d(decimaldecoder_1_dout[22]),
    .c(decimaldecoder_1_dout[21]), .dp(decimaldecoder_1_dout[20]));
  _7_Segment_Display u_7_segment_display_11 (
    .g(decimaldecoder_1_dout[3]), .f(decimaldecoder_1_dout[2]), .a(decimaldecoder_1_dout[1]),
    .b(decimaldecoder_1_dout[0]), .e(decimaldecoder_1_dout[19]), .d(decimaldecoder_1_dout[18]),
    .c(decimaldecoder_1_dout[17]), .dp(decimaldecoder_1_dout[16]));
  _7_Segment_Display u_7_segment_display_12 (
    .g(decimaldecoder_2_dout[3]), .f(decimaldecoder_2_dout[2]), .a(decimaldecoder_2_dout[1]),
    .b(decimaldecoder_2_dout[0]), .e(decimaldecoder_2_dout[19]), .d(decimaldecoder_2_dout[18]),
    .c(decimaldecoder_2_dout[17]), .dp(decimaldecoder_2_dout[16]));
  _7_Segment_Display u_7_segment_display_13 (
    .g(decimaldecoder_3_dout[3]), .f(decimaldecoder_3_dout[2]), .a(decimaldecoder_3_dout[1]),
    .b(decimaldecoder_3_dout[0]), .e(decimaldecoder_3_dout[19]), .d(decimaldecoder_3_dout[18]),
    .c(decimaldecoder_3_dout[17]), .dp(decimaldecoder_3_dout[16]));
  BitSelector #(.group(4)) bitselector_1 (.in(register8bit_1_dout), .out(controlled_buffer_1_out), .sel(1'b0));
  LED D7 (.in(alu_1_dout[7]));
  LED D6 (.in(alu_1_dout[6]));
  LED D5 (.in(alu_1_dout[5]));
  LED D4 (.in(alu_1_dout[4]));
  assign alu_1_dout = OEtestingData ? testingData : 8'bz;  // Controlled_Buffer controlled_buffer_2
  LED D3 (.in(alu_1_dout[3]));
  LED D2 (.in(alu_1_dout[2]));
  LED D1 (.in(alu_1_dout[1]));
  LED DO (.in(alu_1_dout[0]));
  assign alu_1_dout = InternalOE ? MBRcontent : 8'bz;  // Controlled_Buffer controlled_buffer_3
  register8bit register8bit_4 (
    .clk(clk_out), .we(controlunit_1_opwe), .de(alu_1_dout), .oe(controlunit_1_opoe), .Dout(alu_1_dout),
    .Dstored(out_16));
  mar mar_1 (
    .clk(clk_out), .we(controlunit_1_wemar), .din(controlled_buffer_1_out), .oe(controlunit_1_oemar),
    .Dout(mar_1_dout), .Dstored(MARcontent));
  register8bit register8bit_5 (
    .clk(clk_out), .we(controlunit_1_mbrwe), .de(alu_1_dout), .oe(controlunit_1_mbeoe),
    .Dout(register8bit_5_dout), .Dstored(MBRcontent));
  LED Dd7 (.in(alu_1_dout[7]));
  LED Dd6 (.in(alu_1_dout[6]));
  LED Dd5 (.in(alu_1_dout[5]));
  LED Dd4 (.in(alu_1_dout[4]));
  _7_Segment_Display u_7_segment_display_14 (
    .g(decimaldecoder_5_dout[15]), .f(decimaldecoder_5_dout[14]), .a(decimaldecoder_5_dout[13]),
    .b(decimaldecoder_5_dout[12]), .e(decimaldecoder_5_dout_2[15]), .d(decimaldecoder_5_dout_2[14]),
    .c(decimaldecoder_5_dout_2[13]), .dp(decimaldecoder_5_dout_2[12]));
  assign mar_1_dout = OE_test ? OE_testing_data : 4'bz;  // Controlled_Buffer controlled_buffer_4
  LED Dd3 (.in(alu_1_dout[3]));
  LED Dd2 (.in(alu_1_dout[2]));
  LED Dd1 (.in(alu_1_dout[1]));
  LED Dd0 (.in(alu_1_dout[0]));
  _7_Segment_Display u_7_segment_display_15 (
    .g(decimaldecoder_5_dout[11]), .f(decimaldecoder_5_dout[10]), .a(decimaldecoder_5_dout[9]),
    .b(decimaldecoder_5_dout[8]), .e(decimaldecoder_5_dout_2[11]), .d(decimaldecoder_5_dout_2[10]),
    .c(decimaldecoder_5_dout_2[9]), .dp(decimaldecoder_5_dout_2[8]));
  _7_Segment_Display u_7_segment_display_16 (
    .g(decimaldecoder_5_dout[7]), .f(decimaldecoder_5_dout[6]), .a(decimaldecoder_5_dout[5]),
    .b(decimaldecoder_5_dout[4]), .e(decimaldecoder_5_dout_2[7]), .d(decimaldecoder_5_dout_2[6]),
    .c(decimaldecoder_5_dout_2[5]), .dp(decimaldecoder_5_dout_2[4]));
  decimalDecoder decimaldecoder_5 (.Din(out_16), .Dout({decimaldecoder_5_dout_2, decimaldecoder_5_dout}));
  _7_Segment_Display u_7_segment_display_17 (
    .g(decimaldecoder_5_dout[3]), .f(decimaldecoder_5_dout[2]), .a(decimaldecoder_5_dout[1]),
    .b(decimaldecoder_5_dout[0]), .e(decimaldecoder_5_dout_2[3]), .d(decimaldecoder_5_dout_2[2]),
    .c(decimaldecoder_5_dout_2[1]), .dp(decimaldecoder_5_dout_2[0]));
  RAM #(.addrWidth(4)) ram_1 (
    .addr(mar_1_dout), .we(controlunit_1_weram), .oe(controlled_buffer_5_out), .clk(clk_out),
    .din(register8bit_5_dout), .dout(ram_1_dout));
  assign controlled_buffer_5_out = 1'b1 ? controlunit_1_oeram : 1'bz;  // Controlled_Buffer controlled_buffer_5
  assign alu_1_dout = controlled_buffer_5_out ? ram_1_dout : 8'bz;  // Controlled_Buffer controlled_buffer_6

  // Notes on the sheet:
  //   INSTRUCTION REGISTER
  //   ragister A
  //   register B
  //   INTERNAL ADDRESS BUS 4bit
  //   INTERNAL BUS PORT
  //   MAR
  //   MBR
  //   OUTPUT REGISTER
  //   EXTERNAL ADDRESS BUS
  //   EXTERNAL DATA BUS
endmodule

module memory_cell (
  input  clk,
  input  WE,
  input  Din,
  input  OE,
  output Dout,
  output Dstored
);

  wire and_1_out, and_2_out, not_1_out, or_1_out;

  not not_1 (not_1_out, WE);
  and and_1 (and_1_out, Dstored, not_1_out);
  and and_2 (and_2_out, WE, Din);
  or or_1 (or_1_out, and_1_out, and_2_out);
  D_Flip_Flop d_ff_1 (.D(or_1_out), .clk(clk), .Q(Dstored));  // open: Qn, preset, reset
  assign Dout = OE ? Dstored : 1'bz;  // Controlled_Buffer controlled_buffer_1

  // Notes on the sheet:
  //   1 BIT MEMORY CELL
endmodule

module register8bit (
  input  clk,
  input  we,
  input  [7:0] de,
  input  oe,
  output [7:0] Dout,
  output [7:0] Dstored
);

  memory_cell memory_cell_1 (.clk(clk), .WE(we), .Din(de[0]), .OE(oe), .Dout(Dout[0]), .Dstored(Dstored[0]));
  memory_cell memory_cell_2 (.clk(clk), .WE(we), .Din(de[1]), .OE(oe), .Dout(Dout[1]), .Dstored(Dstored[1]));
  memory_cell memory_cell_3 (.clk(clk), .WE(we), .Din(de[2]), .OE(oe), .Dout(Dout[2]), .Dstored(Dstored[2]));
  memory_cell memory_cell_4 (.clk(clk), .WE(we), .Din(de[3]), .OE(oe), .Dout(Dout[3]), .Dstored(Dstored[3]));
  memory_cell memory_cell_5 (.clk(clk), .WE(we), .Din(de[4]), .OE(oe), .Dout(Dout[4]), .Dstored(Dstored[4]));
  memory_cell memory_cell_6 (.clk(clk), .WE(we), .Din(de[5]), .OE(oe), .Dout(Dout[5]), .Dstored(Dstored[5]));
  memory_cell memory_cell_7 (.clk(clk), .WE(we), .Din(de[6]), .OE(oe), .Dout(Dout[6]), .Dstored(Dstored[6]));
  memory_cell memory_cell_8 (.clk(clk), .WE(we), .Din(de[7]), .OE(oe), .Dout(Dout[7]), .Dstored(Dstored[7]));

  // Notes on the sheet:
  //   8 BIT REGISTER
endmodule

module mar (
  input  clk,
  input  we,
  input  [3:0] din,
  input  oe,
  output [3:0] Dout,
  output [3:0] Dstored
);

  memory_cell memory_cell_1 (.clk(clk), .WE(we), .Din(din[0]), .OE(oe), .Dout(Dout[0]), .Dstored(Dstored[0]));
  memory_cell memory_cell_2 (.clk(clk), .WE(we), .Din(din[1]), .OE(oe), .Dout(Dout[1]), .Dstored(Dstored[1]));
  memory_cell memory_cell_3 (.clk(clk), .WE(we), .Din(din[2]), .OE(oe), .Dout(Dout[2]), .Dstored(Dstored[2]));
  memory_cell memory_cell_4 (.clk(clk), .WE(we), .Din(din[3]), .OE(oe), .Dout(Dout[3]), .Dstored(Dstored[3]));

  // Notes on the sheet:
  //   MEMORY ADDRESS FOR REGISTER
endmodule

module ALU (
  input  [7:0] regA,
  input  [7:0] regB,
  input  WE,
  input  [7:0] selectBits,
  input  clk,
  input  OE,
  output [7:0] Dout,
  output [7:0] ALUresult
);

  wire [1:0] bitselector_1_out;
  wire [7:0] adder_1_out, and_1_out, or_1_out, register8bit_1_dstored, register8bit_2_dstored,
       register8bit_3_dstored, subtractor_1_out;

  register8bit register8bit_1 (.clk(clk), .we(WE), .de(regA), .Dstored(register8bit_1_dstored));  // open: oe, Dout
  register8bit register8bit_2 (.clk(clk), .we(WE), .de(regB), .Dstored(register8bit_2_dstored));  // open: oe, Dout
  register8bit register8bit_3 (
    .clk(clk), .we(WE), .de(selectBits), .Dstored(register8bit_3_dstored));  // open: oe, Dout
  BitSelector #(.group(2)) bitselector_1 (.in(register8bit_3_dstored), .out(bitselector_1_out), .sel(2'b00));
  Adder adder_1 (.a(register8bit_1_dstored), .b(register8bit_2_dstored), .out(adder_1_out));  // open: cin, cout
  Subtractor subtractor_1 (
    .a(register8bit_1_dstored), .b(register8bit_2_dstored), .out(subtractor_1_out));  // open: bin, bout
  assign and_1_out = register8bit_1_dstored & register8bit_2_dstored;  // AND_Gate and_1, 8 bits wide
  assign or_1_out = register8bit_1_dstored | register8bit_2_dstored;  // OR_Gate or_1, 8 bits wide
  Multiplexer #(.select(2), .width(8)) multiplexer_1 (
    .in0(adder_1_out), .in1(subtractor_1_out), .in2(and_1_out), .in3(or_1_out), .out(ALUresult),
    .sel(bitselector_1_out));
  assign Dout = OE ? ALUresult : 8'bz;  // Controlled_Buffer controlled_buffer_1
endmodule

module decimalDecoder (
  input  [7:0] Din,
  output [31:0] Dout
);

  ROM #(.dataWidth(32)) rom_1 (
    .addr(Din),
    .data({Dout[31:28], Dout[15:12], Dout[27:24], Dout[11:8], Dout[23:20], Dout[7:4], Dout[19:16], Dout[3:0]}));

  // Notes on the sheet:
  //   contents of rom_1 (hex, n*v repeats v):
  //   e7 21 cb 6b 2d 6e ee 23 ef 2f 21e7 2121 21cb 216b 212d 216e 21ee 2123 21ef 212f cbe7 cb21 cbcb cb6b
  //   cb2d cb6e cbee cb23 cbef cb2f 6be7 6b21 6bcb 6b6b 6b2d 6b6e 6bee 6b23 6bef 6b2f 2de7 2d21 2dcb 2d6b
  //   2d2d 2d6e 2dee 2d23 2def 2d2f 6ee7 6e21 6ecb 6e6b 6e2d 6e6e 6eee 6e23 6eef 6e2f eee7 ee21 eecb ee6b
  //   ee2d ee6e eeee ee23 eeef ee2f 23e7 2321 23cb 236b 232d 236e 23ee 2323 23ef 232f efe7 ef21 efcb ef6b
  //   ef2d ef6e efee ef23 efef ef2f 2fe7 2f21 2fcb 2f6b 2f2d 2f6e 2fee 2f23 2fef 2f2f 21e7e7 21e721 21e7cb
  //   21e76b 21e72d 21e76e 21e7ee 21e723 21e7ef 21e72f 2121e7 212121 2121cb 21216b 21212d 21216e 2121ee
  //   212123 2121ef 21212f 21cbe7 21cb21 21cbcb 21cb6b 21cb2d 21cb6e 21cbee 21cb23 21cbef 21cb2f 216be7
  //   216b21 216bcb 216b6b 216b2d 216b6e 216bee 216b23 216bef 216b2f 212de7 212d21 212dcb 212d6b 212d2d
  //   212d6e 212dee 212d23 212def 212d2f 216ee7 216e21 216ecb 216e6b 216e2d 216e6e 216eee 216e23 216eef
  //   216e2f 21eee7 21ee21 21eecb 21ee6b 21ee2d 21ee6e 21eeee 21ee23 21eeef 21ee2f 2123e7 212321 2123cb
  //   21236b 21232d 21236e 2123ee 212323 2123ef 21232f 21efe7 21ef21 21efcb 21ef6b 21ef2d 21ef6e 21efee
  //   21ef23 21efef 21ef2f 212fe7 212f21 212fcb 212f6b 212f2d 212f6e 212fee 212f23 212fef 212f2f cbe7e7
  //   cbe721 cbe7cb cbe76b cbe72d cbe76e cbe7ee cbe723 cbe7ef cbe72f cb21e7 cb2121 cb21cb cb216b cb212d
  //   cb216e cb21ee cb2123 cb21ef cb212f cbcbe7 cbcb21 cbcbcb cbcb6b cbcb2d cbcb6e cbcbee cbcb23 cbcbef
  //   cbcb2f cb6be7 cb6b21 cb6bcb cb6b6b cb6b2d cb6b6e cb6bee cb6b23 cb6bef cb6b2f cb2de7 cb2d21 cb2dcb
  //   cb2d6b cb2d2d cb2d6e cb2dee cb2d23 cb2def cb2d2f cb6ee7 cb6e21 cb6ecb cb6e6b cb6e2d cb6e6e
  //   DECIMAL DECODER
endmodule

module controlUnit (
  input  en,
  input  [3:0] counter,
  input  ce,
  input  co,
  input  en1,
  input  en0,
  input  sw,
  output weMAR,
  output oeMAR,
  output weRAM,
  output oeRAM,
  output irWE,
  output irOE,
  output aWE,
  output bWE,
  output aluWE,
  output aluOE,
  output mbrWE,
  output mbeOE,
  output opWE,
  output opOE
);

  wire not_1_out, not_2_out, not_3_out, not_4_out, not_5_out, not_6_out, not_7_out, not_8_out, not_9_out,
       not_10_out, or_1_out, or_2_out, or_3_out, or_4_out, or_5_out, or_6_out, or_7_out, or_8_out, or_9_out,
       or_10_out, or_11_out, or_12_out, or_13_out, or_14_out, or_15_out, or_16_out, or_17_out, or_18_out,
       or_19_out, or_20_out, or_21_out, or_22_out, or_23_out, or_24_out, or_25_out;

  not not_1 (not_1_out, en);
  not not_2 (not_2_out, counter[3]);
  not not_3 (not_3_out, counter[2]);
  not not_4 (not_4_out, counter[1]);
  not not_5 (not_5_out, counter[0]);
  not not_6 (not_6_out, ce);
  not not_7 (not_7_out, co);
  not not_8 (not_8_out, en1);
  not not_9 (not_9_out, en0);
  not not_10 (not_10_out, sw);
  or or_1 (or_1_out, co, en0);
  or or_2 (or_2_out, en1, not_9_out);
  or or_3 (or_3_out, not_7_out, not_8_out);
  or or_4 (or_4_out, counter[0], not_10_out);
  or or_5 (or_5_out, ce, not_8_out, not_9_out);
  or or_6 (or_6_out, not_6_out, en1);
  or or_7 (or_7_out, not_6_out, en0);
  or or_8 (or_8_out, en0, not_10_out);
  or or_9 (or_9_out, not_4_out, not_10_out);
  or or_10 (or_10_out, not_8_out, not_10_out);
  or or_11 (or_11_out, ce, not_9_out);
  or or_12 (or_12_out, not_6_out, en0);
  or or_13 (or_13_out, counter[0], not_10_out);
  or or_14 (or_14_out, ce, not_8_out, not_9_out);
  or or_15 (or_15_out, not_6_out, en1);
  or or_16 (or_16_out, not_6_out, en0);
  or or_17 (or_17_out, en0, not_10_out);
  or or_18 (or_18_out, not_4_out, not_10_out);
  or or_19 (or_19_out, not_4_out, not_5_out, not_8_out);
  or or_20 (or_20_out, not_8_out, not_10_out);
  and and_1 (irWE, not_10_out, not_9_out, not_8_out, not_7_out, not_6_out, not_3_out, not_2_out, not_1_out);
  and and_2 (irOE, en1, en0, not_10_out, not_7_out, not_6_out, not_3_out, not_2_out, not_1_out);
  and and_3 (aWE, ce, en1, en0, not_10_out, not_7_out, not_5_out, not_4_out, not_3_out, not_2_out, not_1_out);
  and and_4 (bWE, counter[0], ce, en1, en0, not_10_out, not_7_out, not_4_out, not_3_out, not_2_out, not_1_out);
  and and_5 (aluWE, counter[1], ce, en1, en0, not_10_out, not_7_out, not_5_out, not_3_out, not_2_out, not_1_out);
  and and_6 (aluOE, counter[1], counter[0], en1, en0, not_7_out, not_6_out, not_3_out, not_2_out, not_1_out);
  and and_7 (mbrWE, counter[1], counter[0], en1, en0, not_10_out, not_7_out, not_6_out, not_3_out, not_2_out, not_1_out);
  or or_21 (or_21_out, ce, not_9_out);
  or or_22 (or_22_out, not_6_out, en0);
  and and_8 (opWE, counter[1], counter[0], en1, en0, sw, not_7_out, not_6_out, not_3_out, not_2_out, not_1_out);
  or or_23 (or_23_out, ce, not_9_out);
  or or_24 (or_24_out, not_6_out, en0);
  or or_25 (or_25_out, en1, en0);
  and and_9 (weMAR, not_10_out, not_6_out, not_3_out, not_2_out, not_1_out, or_1_out, or_2_out, or_3_out);
  and and_10 (oeMAR, or_4_out, or_5_out, not_7_out, or_6_out, or_7_out, or_8_out, or_9_out, not_3_out, not_2_out, not_1_out, or_10_out);
  and and_11 (weRAM, counter[1], counter[0], en1, not_10_out, or_11_out, not_7_out, or_12_out, not_3_out, not_2_out, not_1_out);
  and and_12 (oeRAM, or_13_out, or_14_out, not_7_out, or_15_out, or_16_out, or_17_out, or_18_out, or_19_out, not_3_out, not_2_out, not_1_out, or_20_out);
  and and_13 (mbeOE, counter[1], counter[0], en1, not_10_out, or_21_out, not_7_out, or_22_out, not_3_out, not_2_out, not_1_out);
  and and_14 (opOE, counter[1], counter[0], sw, or_23_out, not_7_out, or_24_out, not_3_out, not_2_out, not_1_out, or_25_out);
endmodule

module counterForALU (
  input  [3:0] in_1,
  input  clk,
  output [3:0] out_3
);

  wire and_2_out, and_3_out, not_1_out;
  wire [3:1] counter_1_q;

  Counter #(.max('h5), .width(4)) counter_1 (
    .D(in_1), .Q({counter_1_q, out_3[0]}), .clk(clk));  // open: load, count, carry, up, clr
  and and_1 (out_3[3], out_3[0], counter_1_q[2]);
  not not_1 (not_1_out, counter_1_q[1]);
  nor nor_1 (out_3[2], out_3[0], counter_1_q[1], counter_1_q[2], counter_1_q[3]);
  and and_2 (and_2_out, out_3[0], counter_1_q[1]);
  or or_1 (out_3[1], and_2_out, and_3_out);
  and and_3 (and_3_out, not_1_out, counter_1_q[2]);
endmodule
